# Fritzing sketch nightlight (saved by Fritzing 0.8.5b)
circuit board: 5cm x 4.5cm
breadboards: 1

parts:
  U1 = MCP1702 Voltage Regulator [package="TO92 [THT]"]
  IC1 = ATtiny85 [package=DIL]
  R1 = Resistor [tolerance=±5% resistance=10k package=THT]
  R2 = Resistor [tolerance=±5% resistance=10k package=THT]
  V+ = male pin header, 1 pin [form="♂ (male)"]
  V- = male pin header, 1 pin [form="♂ (male)"]
  R4 = Resistor [tolerance=±5% resistance=10k package=THT]
  LED1 = LED - 5mm [color="Red (633nm)" package="5 mm [THT]"]
  R5 = Resistor [tolerance=±5% resistance=68 package=THT]
  R6 = Resistor [tolerance=±5% resistance=10k package=THT]
  Q1 = NPN-Transistor [part_number=BC547 package="TO92 [THT]"]
  R7 = Resistor [tolerance=±5% resistance=10k package=THT]
  D1 = Rectifier Diode [part_number=1N4001 package="300 mil [THT]"]
  R9 = Resistor [tolerance=±5% resistance=10k package=THT]
  LDR = male pin header, 2 pins [form="♂ (male)"]
  Q2 = NPN-Transistor [package="TO92 [THT]"]
  D2 = Rectifier Diode [part_number=1N4001 package="300 mil [THT]"]
  PIR = male pin header, 3 pins [form="♂ (male)"]
  LAMP = male pin header, 2 pins [form="♂ (male)"]
  SERIAL = male pin header, 6 pins [form="♂ (male)"]
  C1 = Ceramic Capacitor [capacitance=100nF package="200 mil [THT, multilayer]"]
  C2 = Ceramic Capacitor [capacitance=100nF package="200 mil [THT, multilayer]"]

nets:
  GND: U1.GND, IC1.GND, R2.Pin_1, V-.pin1, LED1.cathode, R9.Pin_1, LDR.pin2, Q2.E, PIR.pin2, SERIAL.pin1, C1.0, C2.0
  N1: U1.Vin, R1.Pin_0, V+.pin1, D2.anode, C2.1
  VCC: U1.Vout, IC1.VCC, R6.Pin_0, C1.1
  N2: IC1.PB5/RESET, R6.Pin_1
  VBAT: IC1.PB3, R1.Pin_1, R2.Pin_0
  VMON: IC1.PB4, R4.Pin_1, R9.Pin_0, LDR.pin1
  LAMP: IC1.PB0/SDA/MOSI, Q2.B
  N3: IC1.PB1/MISO, R5.Pin_0
  DATA: IC1.PB2/SCL/SCK, Q1.E, D1.anode
  N4: R4.Pin_0, PIR.pin3
  N5: LED1.anode, R5.Pin_1
  N6: Q1.B, R7.Pin_1
  RX: Q1.C, SERIAL.pin4
  TX: R7.Pin_0, D1.cathode, SERIAL.pin5
  N7: Q2.C, LAMP.pin2
  VRAW: D2.cathode, PIR.pin1, LAMP.pin1

notes:
  The Garage Lab, Motion controlled night light., 1B
  GND

custom parts:
  MCP1702 Voltage Regulator: A MCP1702 Low Dropout Fixed Voltage Regulator (available in 1.2V, 1.5V, 1.8V, 2.5V, 2.8V, 3.0V, 3.3V, 4.0V, 5.0V)
